# Fritzing sketch ProjektRFIDServoLEDdiode - 2RFID (saved by Fritzing 0.9.3b)
breadboards: 1

parts:
  Part1 = Arduino Mega 2560 (Rev3)
  R1 = Resistor [tolerance=±5% resistance=220 package=THT]
  R3 = Resistor [tolerance=±5% resistance=220 package=THT]
  napred = LED - 5mm [color="Red (633nm)" package="5 mm [THT]"]
  iza = LED - 5mm [color="Red (633nm)" package="5 mm [THT]"]
  J1 = Basic Servo
  Part2 = RFID-RC522-v2
  Part3 = RFID-RC522-v2
  BAT1 = Battery Holders [package=lipo-1100mAh]
  Part7 = Pololu 12V Step-Down Regulator
  Part8 = Pololu 12V Step-Down Regulator

nets:
  5V: Part1.5V, J1.vcc
  GND: Part1.GND, napred.cathode, iza.cathode, J1.gnd, Part2.GND, Part3.GND, BAT1.-, Part7.GND, Part8.GND
  N1: Part1.D2_PWM, Part2.SDA
  N2: Part1.D3_PWM, Part3.SDA
  N3: Part1.D5_PWM, J1.pulse
  N4: Part1.D22, R3.Pin_0
  N5: Part1.D23, R1.Pin_0
  N6: Part1.D29, Part2.RST
  N7: Part1.D34, Part3.RST
  N8: Part1.D50, Part2.MISO, Part3.MISO
  N9: Part1.D51, Part2.MOSI, Part3.MOSI
  N10: Part1.D52, Part2.SCK, Part3.SCK
  N11: R1.Pin_1, napred.anode
  N12: R3.Pin_1, iza.anode
  N13: Part2.3.3V, Part8.VOUT
  N14: Part3.3.3V, Part7.VOUT
  VIN: BAT1.+, Part7.VIN, Part8.VIN

custom parts:
  RFID-RC522-v2: A simple China made RFID-RC522 Reader; do check the pin labels, as this is a MFRC522 based clone.
